# Fritzing sketch Sketch (saved by Fritzing 0.9.3b)
breadboards: 2

parts:
  元件1 = Arduino Uno (Rev3)
  Disp1 = LBT2088AH [part_number=LBT2088AH]
  hc-sr1 = hc-sr04

nets:
  N1: 元件1.A0, Disp1.pin_6
  N2: 元件1.A1, Disp1.pin_11
  N3: 元件1.A2, Disp1.pin_15
  N4: 元件1.A3, Disp1.pin_16
  N5: 元件1.A4/SDA, hc-sr1.Trig
  N6: 元件1.A5/SCL, hc-sr1.Echo
  N7: 元件1.D8, Disp1.pin_14
  N8: 元件1.D9_PWM, Disp1.pin_9
  N9: 元件1.D10_PWM/SS, Disp1.pin_13
  N10: 元件1.D11_PWM/MOSI, Disp1.pin_3
  N11: 元件1.D12/MISO, Disp1.pin_4
  N12: 元件1.D13/SCK, Disp1.pin_10
  N13: 元件1.D2, Disp1.pin_5
  N14: 元件1.D3_PWM, Disp1.pin2
  N15: 元件1.D4, Disp1.pin_7
  N16: 元件1.D5_PWM, Disp1.pin1
  N17: 元件1.D6_PWM, Disp1.pin_12
  N18: 元件1.D7, Disp1.pin_8
  5V: 元件1.5V, hc-sr1.VCC
  GND: 元件1.GND, hc-sr1.GND

notes:
  1 7
  2 4
  3 a0
  4 2
  5 12
  6 11
  7 3
  8 5
  1 9
  2 13
  3 a1
  4 6
  5 10
  6 8
  7 a2
  8 a3

// code stored in the sketch: main.ino
#include <avr/pgmspace.h>
#include <SoftwareSerial.h>
#include <Wire.h>
#include <math.h>
const int line[]={2,3,4,5,6,7,8,9};
const int column[]={10,11,12,13,A0,A1,A2,A3};
//using flash memory
const bool frame[8][40] PROGMEM={
    {0,0,0,0,0,0,0,0,0,1,0,0,0,0,0,0,0,0,0,0,0,0,0,0,0,0,0,0,0,0,0,0,0,0,0,0,0,0,0,0},
    {0,0,1,1,1,1,0,0,1,1,1,0,0,0,0,0,0,0,0,0,0,0,0,0,0,0,1,0,0,0,1,1,1,0,0,0,0,0,0,0},
    {0,0,1,0,1,1,1,0,1,1,0,0,0,0,1,1,1,0,0,0,1,1,1,0,0,1,1,0,0,1,0,0,0,1,0,0,0,0,0,0},
    {0,0,1,0,0,1,1,0,0,1,0,0,0,1,1,1,1,1,0,1,1,1,1,1,0,0,1,0,0,1,1,1,1,1,0,0,0,0,0,0},
    {0,0,1,1,1,1,1,0,0,1,0,0,0,1,0,0,0,1,0,1,0,0,0,1,0,0,1,0,0,1,0,0,0,1,0,0,0,0,0,0},
    {0,0,1,1,1,1,1,0,0,1,0,0,0,1,1,1,1,1,0,1,1,1,1,1,0,0,1,0,0,1,0,0,0,1,0,0,0,0,0,0},
    {0,0,1,1,1,1,1,0,1,1,1,0,0,1,0,0,0,1,0,1,0,0,0,1,0,0,1,0,0,0,1,1,1,1,0,0,0,0,0,0},
    {0,0,0,0,0,0,0,0,0,0,0,0,0,1,1,1,1,1,0,1,1,1,1,1,1,1,1,1,1,0,0,0,0,0,0,0,0,0,0,0}
};
bool playground[8][8]={
    {0,0,0,0,0,0,0,0},
    {0,0,0,0,0,0,0,0},
    {0,0,0,0,0,0,0,0},
    {0,0,0,0,0,0,0,0},
    {0,0,0,0,0,0,0,0},
    {0,0,0,0,0,0,0,0},
    {0,0,0,0,0,0,0,0},
    {0,0,0,0,0,0,0,0}
};
double pos=0.0;
int led_displayID=0;
int trig=A4;
int echo=A5;
void def_display();
//void bluetooth();
void sec_display();
long duration;
int distance;
int supersonic_func1();
void setup() {
    Serial.begin(9600);
    pinMode(trig,OUTPUT);
    pinMode(echo,INPUT);
	for(int i=0;i<8;i++){
        pinMode(line[i],OUTPUT);
        pinMode(column[i],OUTPUT);
        digitalWrite(line[i],LOW);
        digitalWrite(column[i],HIGH);
    }
    Serial.println("[_INIT_]");
}
void loop() {
    switch (led_displayID){
        case 0:
            def_display();
            break;
        case 1:
            //bluetooth();
            sec_display();
            delay(2);
            break;
        default:
            break;
    }
}
void def_display(){
    for(int l=0;l<8;l++){
        for(int c=0;c<8;c++){
            int frame_buf=pgm_read_byte_near(&frame[c][l+(int)(floor(pos))]);
            Serial.print(frame_buf);
            Serial.print(" ");
            if(frame_buf==1){
                digitalWrite(line[l],HIGH);
                digitalWrite(column[c],LOW);
                delay(1);
                digitalWrite(line[l],LOW);
                digitalWrite(column[c],HIGH);
            }else if(frame_buf==0){
                delay(1);
            }
            pos+=0.02;
        }
        Serial.println("");
    }
    Serial.println("--------------------");
    if(pos>=39.0){
        pos=0.0;
        led_displayID=1;
    }
    /*if(bt.available()){
        led_displayID=1;
        Serial.println("[_DISPLAYID=1_]");
        pos=0.0;
    }*/
}
void sec_display(){
    for(int l=0;l<8;l++){
        for(int c=0;c<8;c++){
            int buffer=playground[c][l];
            switch (buffer){
                case 1:
                    digitalWrite(line[l],HIGH);
                    digitalWrite(column[c],LOW);
                    delay(1);
                    digitalWrite(line[l],LOW);
                    digitalWrite(column[c],HIGH);
                    break;
                case 0:
                    delay(1);
                    break;
                default:
                    break;
                }
        }
    }
    int display_bar=supersonic_func1();
    if(display_bar>100){
        display_bar=100;
    }
    display_bar=display_bar/12;
    for(int i=0;i<8;i++){
        for(int j=0;j<8;j++){
            if(j<7){
                playground[i][j]=playground[i][j+1];
            }
        }
        if((8-i)<=display_bar){
            playground[i][7]=1;
        }else{
            playground[i][7]=0;
        }
    }
}
int supersonic_func1(){
    digitalWrite(trig,LOW);
    delayMicroseconds(2);
    digitalWrite(trig,HIGH);
    delayMicroseconds(10);
    digitalWrite(trig,LOW);
    /*
    v=340 m/s
    t=s/v
    s=t*0.034/2
    */
    duration=pulseIn(echo,HIGH);
    distance=duration*0.034/2;
    Serial.println(distance);
    return(distance);
}
/*END*/
/*const int frame[8][40]={
    {0,0,0,0,0,0,0,0,0,0,0,0,0,0,0,0,0,0,0,0,0,0,0,0,0,0,0,0,0,0,0,0,0,0,0,0,0,0,0,0},
    {0,0,0,0,0,0,0,0,0,0,0,0,0,0,0,0,0,0,0,0,0,0,0,0,0,0,0,0,0,0,0,0,0,0,0,0,0,0,0,0},
    {0,0,0,0,0,0,0,0,0,0,0,0,0,0,0,0,0,0,0,0,0,0,0,0,0,0,0,0,0,0,0,0,0,0,0,0,0,0,0,0},
    {0,0,0,0,0,0,0,0,0,0,0,0,0,0,0,0,0,0,0,0,0,0,0,0,0,0,0,0,0,0,0,0,0,0,0,0,0,0,0,0},
    {0,0,0,0,0,0,0,0,0,0,0,0,0,0,0,0,0,0,0,0,0,0,0,0,0,0,0,0,0,0,0,0,0,0,0,0,0,0,0,0},
    {0,0,0,0,0,0,0,0,0,0,0,0,0,0,0,0,0,0,0,0,0,0,0,0,0,0,0,0,0,0,0,0,0,0,0,0,0,0,0,0},
    {0,0,0,0,0,0,0,0,0,0,0,0,0,0,0,0,0,0,0,0,0,0,0,0,0,0,0,0,0,0,0,0,0,0,0,0,0,0,0,0},
    {0,0,0,0,0,0,0,0,0,0,0,0,0,0,0,0,0,0,0,0,0,0,0,0,0,0,0,0,0,0,0,0,0,0,0,0,0,0,0,0}
}*/
/*void bluetooth(){
    if(bt.available()){
        /*do something*/
    /*    
    }else if(!bt.available()){
        delay(2);
    }
}*/
